// Logisim project CPUjmp.circ as structural Verilog: 2 circuits, main circuit main
module main (
  input  ZR,
  input  NG,
  input  j1,
  input  j2,
  input  j3,
  output out_6
);

  wire and_1_out, and_2_out, not_1_out, or_1_out, or_2_out;

  and and_1 (and_1_out, ~ZR, ~NG);  // AND_Gate
  not not_1 (not_1_out, ZR);
  or or_1 (or_1_out, ZR, ~NG);  // OR_Gate
  and and_2 (and_2_out, ~ZR, NG);  // AND_Gate
  or or_2 (or_2_out, ZR, NG);
  Multiplexer #(.select(3), .enable("false")) multiplexer_1 (
    .in0(1'b0), .in1(and_1_out), .in2(ZR), .in3(or_1_out), .in4(and_2_out), .in5(not_1_out), .in6(or_2_out),
    .in7(1'b1), .out(out_6), .sel({j1, j2, j3}));
endmodule

module main2 (
  input  ZR,
  input  NG,
  input  j1,
  input  j2,
  input  j3,
  output x
);

  wire and_1_out, and_2_out, and_3_out, not_1_out, not_2_out, not_3_out;

  not not_1 (not_1_out, ZR);
  not not_2 (not_2_out, NG);
  not not_3 (not_3_out, ZR);
  and and_1 (and_1_out, not_1_out, not_2_out, j3);
  and and_2 (and_2_out, not_3_out, NG, j1);
  and and_3 (and_3_out, ZR, j2);
  or or_1 (x, and_1_out, and_2_out, and_3_out);
endmodule
